// Logisim project DD1_proj2_final.circ as structural Verilog: 2 circuits, main circuit main
module main (
  input  in_1,
  input  [2:0] in_2,
  input  [3:0] in_3,
  input  [5:0] in_4,
  input  [1:0] in_5
);

  wire and_1_out, and_2_out, and_3_out, and_4_out, and_5_out, and_6_out, and_7_out, and_8_out, and_9_out,
       and_10_out, bcd_to_7_segment_decoder_1_p1, bcd_to_7_segment_decoder_1_p2,
       bcd_to_7_segment_decoder_1_p3, bcd_to_7_segment_decoder_1_p4, bcd_to_7_segment_decoder_1_p6,
       bcd_to_7_segment_decoder_1_p7, bcd_to_7_segment_decoder_1_p8, bcd_to_7_segment_decoder_2_p1,
       bcd_to_7_segment_decoder_2_p2, bcd_to_7_segment_decoder_2_p3, bcd_to_7_segment_decoder_2_p4,
       bcd_to_7_segment_decoder_2_p6, bcd_to_7_segment_decoder_2_p7, bcd_to_7_segment_decoder_2_p8,
       bcd_to_7_segment_decoder_3_p1, bcd_to_7_segment_decoder_3_p2, bcd_to_7_segment_decoder_3_p3,
       bcd_to_7_segment_decoder_3_p4, bcd_to_7_segment_decoder_3_p6, bcd_to_7_segment_decoder_3_p7,
       bcd_to_7_segment_decoder_3_p8, bcd_to_7_segment_decoder_4_p1, bcd_to_7_segment_decoder_4_p2,
       bcd_to_7_segment_decoder_4_p3, bcd_to_7_segment_decoder_4_p4, bcd_to_7_segment_decoder_4_p6,
       bcd_to_7_segment_decoder_4_p7, bcd_to_7_segment_decoder_4_p8, bcd_to_7_segment_decoder_5_p1,
       bcd_to_7_segment_decoder_5_p2, bcd_to_7_segment_decoder_5_p3, bcd_to_7_segment_decoder_5_p4,
       bcd_to_7_segment_decoder_5_p6, bcd_to_7_segment_decoder_5_p7, bcd_to_7_segment_decoder_5_p8,
       bcd_to_7_segment_decoder_6_p1, bcd_to_7_segment_decoder_6_p2, bcd_to_7_segment_decoder_6_p3,
       bcd_to_7_segment_decoder_6_p4, bcd_to_7_segment_decoder_6_p6, bcd_to_7_segment_decoder_6_p7,
       bcd_to_7_segment_decoder_6_p8, bcd_to_7_segment_decoder_7_p2, bcd_to_7_segment_decoder_7_p3,
       bcd_to_7_segment_decoder_7_p4, bcd_to_7_segment_decoder_7_p5, bcd_to_7_segment_decoder_7_p6,
       bcd_to_7_segment_decoder_7_p8, bcd_to_7_segment_decoder_7_p9, bcd_to_7_segment_decoder_7_p10,
       bcd_to_7_segment_decoder_8_p1, bcd_to_7_segment_decoder_8_p2, bcd_to_7_segment_decoder_8_p3,
       bcd_to_7_segment_decoder_8_p4, bcd_to_7_segment_decoder_8_p6, bcd_to_7_segment_decoder_8_p7,
       bcd_to_7_segment_decoder_8_p8, bcd_to_7_segment_decoder_9_p2, bcd_to_7_segment_decoder_9_p3,
       bcd_to_7_segment_decoder_9_p4, bcd_to_7_segment_decoder_9_p5, bcd_to_7_segment_decoder_9_p6,
       bcd_to_7_segment_decoder_9_p8, bcd_to_7_segment_decoder_9_p9, bcd_to_7_segment_decoder_9_p10,
       bcd_to_7_segment_decoder_10_p1, bcd_to_7_segment_decoder_10_p2, bcd_to_7_segment_decoder_10_p3,
       bcd_to_7_segment_decoder_10_p4, bcd_to_7_segment_decoder_10_p6, bcd_to_7_segment_decoder_10_p7,
       bcd_to_7_segment_decoder_10_p8, BTNC_out, clock_1_out, clock_2_out, decoder_1_out0, decoder_1_out1,
       decoder_1_out2, decoder_1_out3, or_1_out, or_2_out, or_3_out, or_4_out, or_5_out, or_6_out, t_ff_1_q,
       t_ff_1_qn, t_ff_2_q;
  wire [1:0] counter_3_q, counter_7_q;
  wire [2:0] counter_1_q, counter_2_q;
  wire [3:0] bcd_to_7_segment_decoder_4_p5, bcd_to_7_segment_decoder_6_p5, bcd_to_7_segment_decoder_8_p5,
       bcd_to_7_segment_decoder_10_p5, counter_4_q, counter_5_q, counter_6_q, multiplexer_1_out;
  wire [5:0] freqdivider_q;

  Clock clock_1 (.out(clock_1_out));
  T_Flip_Flop t_ff_1 (.T(BTNC_out), .clk(BTNC_out), .Q(t_ff_1_q), .Qn(t_ff_1_qn));  // open: reset, preset
  LED led_1 (.in(t_ff_1_qn));
  or or_1 (or_1_out, in_1, and_4_out, and_2_out);
  or or_2 (or_2_out, in_1, and_3_out);
  Counter #(.max('h7), .width(3)) counter_1 (
    .clr(in_1), .load(or_2_out), .count(and_5_out), .clk(t_ff_2_q), .D(in_2), .Q(counter_1_q));  // open: up, carry
  Counter #(.max('h7), .width(3)) counter_2 (
    .clr(in_1), .load(or_3_out), .count(and_6_out), .clk(t_ff_2_q), .D(in_2), .Q(counter_2_q));  // open: up, carry
  Counter #(.max('h3), .width(2)) counter_3 (
    .clr(in_1), .load(or_1_out), .count(and_7_out), .clk(t_ff_2_q), .D(in_5), .Q(counter_3_q));  // open: up, carry
  or or_3 (or_3_out, in_1, and_1_out);
  and and_1 (and_1_out, counter_2_q[0], counter_2_q[2], and_6_out);
  and and_2 (and_2_out, and_7_out, counter_3_q[1]);
  and and_3 (and_3_out, counter_1_q[0], counter_1_q[2], and_5_out);
  and and_4 (and_4_out, counter_3_q[1], counter_6_q[0], counter_6_q[2]);
  or or_4 (or_4_out, in_1, and_5_out);
  or or_5 (or_5_out, in_1, and_6_out);
  or or_6 (or_6_out, in_1, and_4_out, and_7_out);
  Counter #(.max('hf), .width(4)) counter_4 (
    .clr(in_1), .load(or_4_out), .count(t_ff_1_q), .clk(t_ff_2_q), .D(in_3), .Q(counter_4_q));  // open: up, carry
  Counter #(.max('hf), .width(4)) counter_5 (
    .clr(in_1), .load(or_5_out), .count(and_3_out), .clk(t_ff_2_q), .D(in_3), .Q(counter_5_q));  // open: up, carry
  Counter #(.max('hf), .width(4)) counter_6 (
    .clr(in_1), .load(or_6_out), .count(and_1_out), .clk(t_ff_2_q), .D(in_3), .Q(counter_6_q));  // open: up, carry
  and and_5 (and_5_out, counter_4_q[0], counter_4_q[3]);
  and and_6 (and_6_out, and_3_out, counter_5_q[0], counter_5_q[3]);
  and and_7 (and_7_out, and_1_out, counter_6_q[0], counter_6_q[3]);
  // BCD_to_7_Segment_decoder bcd_to_7_segment_decoder_1: pin names not known; wires that end beside it: bcd_to_7_segment_decoder_1_p1, bcd_to_7_segment_decoder_1_p2, bcd_to_7_segment_decoder_1_p3, bcd_to_7_segment_decoder_1_p4, {2'b00, counter_3_q}, bcd_to_7_segment_decoder_1_p6, bcd_to_7_segment_decoder_1_p7, bcd_to_7_segment_decoder_1_p8
  _7_Segment_Display u_7_segment_display_1 (
    .g(bcd_to_7_segment_decoder_1_p1), .f(bcd_to_7_segment_decoder_1_p3), .a(bcd_to_7_segment_decoder_1_p6),
    .b(bcd_to_7_segment_decoder_1_p8), .e(bcd_to_7_segment_decoder_1_p2), .d(bcd_to_7_segment_decoder_1_p4),
    .c(bcd_to_7_segment_decoder_1_p7));  // open: dp
  // BCD_to_7_Segment_decoder bcd_to_7_segment_decoder_2: pin names not known; wires that end beside it: bcd_to_7_segment_decoder_2_p1, bcd_to_7_segment_decoder_2_p2, bcd_to_7_segment_decoder_2_p3, bcd_to_7_segment_decoder_2_p4, counter_6_q, bcd_to_7_segment_decoder_2_p6, bcd_to_7_segment_decoder_2_p7, bcd_to_7_segment_decoder_2_p8
  _7_Segment_Display u_7_segment_display_2 (
    .g(bcd_to_7_segment_decoder_2_p1), .f(bcd_to_7_segment_decoder_2_p3), .a(bcd_to_7_segment_decoder_2_p6),
    .b(bcd_to_7_segment_decoder_2_p8), .e(bcd_to_7_segment_decoder_2_p2), .d(bcd_to_7_segment_decoder_2_p4),
    .c(bcd_to_7_segment_decoder_2_p7), .dp(and_8_out));
  Counter #(.max('h3f), .width(6)) freqdivider (
    .load(and_9_out), .count(1'b1), .clk(clock_1_out), .D(in_4), .Q(freqdivider_q));  // open: clr, up, carry
  // BCD_to_7_Segment_decoder bcd_to_7_segment_decoder_3: pin names not known; wires that end beside it: bcd_to_7_segment_decoder_3_p1, bcd_to_7_segment_decoder_3_p2, bcd_to_7_segment_decoder_3_p3, bcd_to_7_segment_decoder_3_p4, {1'b0, counter_2_q}, bcd_to_7_segment_decoder_3_p6, bcd_to_7_segment_decoder_3_p7, bcd_to_7_segment_decoder_3_p8
  and and_8 (and_8_out, t_ff_1_q, t_ff_2_q);
  _7_Segment_Display u_7_segment_display_3 (
    .g(bcd_to_7_segment_decoder_3_p1), .f(bcd_to_7_segment_decoder_3_p3), .a(bcd_to_7_segment_decoder_3_p6),
    .b(bcd_to_7_segment_decoder_3_p8), .e(bcd_to_7_segment_decoder_3_p2), .d(bcd_to_7_segment_decoder_3_p4),
    .c(bcd_to_7_segment_decoder_3_p7));  // open: dp
  // BCD_to_7_Segment_decoder bcd_to_7_segment_decoder_4: pin names not known; wires that end beside it: bcd_to_7_segment_decoder_4_p1, bcd_to_7_segment_decoder_4_p2, bcd_to_7_segment_decoder_4_p3, bcd_to_7_segment_decoder_4_p4, bcd_to_7_segment_decoder_4_p5, bcd_to_7_segment_decoder_4_p6, bcd_to_7_segment_decoder_4_p7, bcd_to_7_segment_decoder_4_p8
  // BCD_to_7_Segment_decoder bcd_to_7_segment_decoder_5: pin names not known; wires that end beside it: bcd_to_7_segment_decoder_5_p1, bcd_to_7_segment_decoder_5_p2, bcd_to_7_segment_decoder_5_p3, bcd_to_7_segment_decoder_5_p4, counter_5_q, bcd_to_7_segment_decoder_5_p6, bcd_to_7_segment_decoder_5_p7, bcd_to_7_segment_decoder_5_p8
  _7_Segment_Display u_7_segment_display_4 (
    .g(bcd_to_7_segment_decoder_4_p1), .f(bcd_to_7_segment_decoder_4_p3), .a(bcd_to_7_segment_decoder_4_p6),
    .b(bcd_to_7_segment_decoder_4_p8), .e(bcd_to_7_segment_decoder_4_p2), .d(bcd_to_7_segment_decoder_4_p4),
    .c(bcd_to_7_segment_decoder_4_p7));  // open: dp
  and and_9 (and_9_out, freqdivider_q[0], freqdivider_q[1], freqdivider_q[2], freqdivider_q[3], freqdivider_q[4], freqdivider_q[5]);
  _7_Segment_Display u_7_segment_display_5 (
    .g(bcd_to_7_segment_decoder_5_p1), .f(bcd_to_7_segment_decoder_5_p3), .a(bcd_to_7_segment_decoder_5_p6),
    .b(bcd_to_7_segment_decoder_5_p8), .e(bcd_to_7_segment_decoder_5_p2), .d(bcd_to_7_segment_decoder_5_p4),
    .c(bcd_to_7_segment_decoder_5_p7));  // open: dp
  // BCD_to_7_Segment_decoder bcd_to_7_segment_decoder_6: pin names not known; wires that end beside it: bcd_to_7_segment_decoder_6_p1, bcd_to_7_segment_decoder_6_p2, bcd_to_7_segment_decoder_6_p3, bcd_to_7_segment_decoder_6_p4, bcd_to_7_segment_decoder_6_p5, bcd_to_7_segment_decoder_6_p6, bcd_to_7_segment_decoder_6_p7, bcd_to_7_segment_decoder_6_p8
  // BCD_to_7_Segment_decoder bcd_to_7_segment_decoder_7: pin names not known; wires that end beside it: {1'b0, counter_1_q}, bcd_to_7_segment_decoder_7_p2, bcd_to_7_segment_decoder_7_p3, bcd_to_7_segment_decoder_7_p4, bcd_to_7_segment_decoder_7_p5, bcd_to_7_segment_decoder_7_p6, bcd_to_7_segment_decoder_7_p6, bcd_to_7_segment_decoder_7_p8, bcd_to_7_segment_decoder_7_p9, bcd_to_7_segment_decoder_7_p10
  _7_Segment_Display u_7_segment_display_6 (
    .g(bcd_to_7_segment_decoder_6_p1), .f(bcd_to_7_segment_decoder_6_p3), .a(bcd_to_7_segment_decoder_6_p6),
    .b(bcd_to_7_segment_decoder_6_p8), .e(bcd_to_7_segment_decoder_6_p2), .d(bcd_to_7_segment_decoder_6_p4),
    .c(bcd_to_7_segment_decoder_6_p7), .dp(and_10_out));
  T_Flip_Flop t_ff_2 (.T(and_9_out), .clk(clock_1_out), .Q(t_ff_2_q));  // open: Qn, reset, preset
  _7_Segment_Display u_7_segment_display_7 (
    .g(bcd_to_7_segment_decoder_7_p2), .f(bcd_to_7_segment_decoder_7_p4), .a(bcd_to_7_segment_decoder_7_p8),
    .b(bcd_to_7_segment_decoder_7_p10), .e(bcd_to_7_segment_decoder_7_p3), .d(bcd_to_7_segment_decoder_7_p5),
    .c(bcd_to_7_segment_decoder_7_p9));  // open: dp
  and and_10 (and_10_out, t_ff_2_q, t_ff_1_q, decoder_1_out2);
  Button BTNC (.out(BTNC_out));
  // BCD_to_7_Segment_decoder bcd_to_7_segment_decoder_8: pin names not known; wires that end beside it: bcd_to_7_segment_decoder_8_p1, bcd_to_7_segment_decoder_8_p2, bcd_to_7_segment_decoder_8_p3, bcd_to_7_segment_decoder_8_p4, bcd_to_7_segment_decoder_8_p5, bcd_to_7_segment_decoder_8_p6, bcd_to_7_segment_decoder_8_p7, bcd_to_7_segment_decoder_8_p8
  Clock clock_2 (.out(clock_2_out));
  // BCD_to_7_Segment_decoder bcd_to_7_segment_decoder_9: pin names not known; wires that end beside it: counter_4_q, bcd_to_7_segment_decoder_9_p2, bcd_to_7_segment_decoder_9_p3, bcd_to_7_segment_decoder_9_p4, bcd_to_7_segment_decoder_9_p5, bcd_to_7_segment_decoder_9_p6, bcd_to_7_segment_decoder_9_p6, bcd_to_7_segment_decoder_9_p8, bcd_to_7_segment_decoder_9_p9, bcd_to_7_segment_decoder_9_p10
  _7_Segment_Display u_7_segment_display_8 (
    .g(bcd_to_7_segment_decoder_8_p1), .f(bcd_to_7_segment_decoder_8_p3), .a(bcd_to_7_segment_decoder_8_p6),
    .b(bcd_to_7_segment_decoder_8_p8), .e(bcd_to_7_segment_decoder_8_p2), .d(bcd_to_7_segment_decoder_8_p4),
    .c(bcd_to_7_segment_decoder_8_p7));  // open: dp
  _7_Segment_Display u_7_segment_display_9 (
    .g(bcd_to_7_segment_decoder_9_p2), .f(bcd_to_7_segment_decoder_9_p4), .a(bcd_to_7_segment_decoder_9_p8),
    .b(bcd_to_7_segment_decoder_9_p10), .e(bcd_to_7_segment_decoder_9_p3), .d(bcd_to_7_segment_decoder_9_p5),
    .c(bcd_to_7_segment_decoder_9_p9));  // open: dp
  // BCD_to_7_Segment_decoder bcd_to_7_segment_decoder_10: pin names not known; wires that end beside it: bcd_to_7_segment_decoder_10_p1, bcd_to_7_segment_decoder_10_p2, bcd_to_7_segment_decoder_10_p3, bcd_to_7_segment_decoder_10_p4, bcd_to_7_segment_decoder_10_p5, bcd_to_7_segment_decoder_10_p6, bcd_to_7_segment_decoder_10_p7, bcd_to_7_segment_decoder_10_p8
  _7_Segment_Display u_7_segment_display_10 (
    .g(bcd_to_7_segment_decoder_10_p1), .f(bcd_to_7_segment_decoder_10_p3),
    .a(bcd_to_7_segment_decoder_10_p6), .b(bcd_to_7_segment_decoder_10_p8),
    .e(bcd_to_7_segment_decoder_10_p2), .d(bcd_to_7_segment_decoder_10_p4), .c(bcd_to_7_segment_decoder_10_p7));  // open: dp
  Counter #(.max('h3), .width(2)) counter_7 (
    .count(t_ff_1_q), .clk(clock_2_out), .Q(counter_7_q));  // open: clr, load, up, D, carry
  Multiplexer #(.select(2), .width(4)) multiplexer_1 (
    .in0(counter_5_q), .in1({1'b0, counter_2_q}), .in2(counter_6_q), .in3({2'b00, counter_3_q}),
    .out(multiplexer_1_out), .sel(counter_7_q));
  Decoder #(.select(2)) decoder_1 (
    .out0(decoder_1_out0), .out1(decoder_1_out1), .out2(decoder_1_out2), .out3(decoder_1_out3),
    .sel(counter_7_q));  // open: en
  Multiplexer #(.width(4)) multiplexer_2 (
    .in1(multiplexer_1_out), .out(bcd_to_7_segment_decoder_4_p5), .sel(decoder_1_out3));  // open: in0
  Multiplexer #(.width(4)) multiplexer_3 (
    .in1(multiplexer_1_out), .out(bcd_to_7_segment_decoder_6_p5), .sel(decoder_1_out2));  // open: in0
  Multiplexer #(.width(4)) multiplexer_4 (
    .in1(multiplexer_1_out), .out(bcd_to_7_segment_decoder_8_p5), .sel(decoder_1_out1));  // open: in0
  Multiplexer #(.width(4)) multiplexer_5 (
    .in1(multiplexer_1_out), .out(bcd_to_7_segment_decoder_10_p5), .sel(decoder_1_out0));  // open: in0
endmodule

module clockdiv (
  input  clockout,
  input  clockin
);

  wire and_1_out, and_2_out, and_3_out, and_4_out, and_5_out, not_1_out, not_2_out, t_ff_1_q, t_ff_2_q,
       t_ff_3_q, t_ff_4_q, t_ff_5_q, t_ff_6_q;
  wire [1:0] counter_1_q;

  Counter #(.max('h3), .width(2)) counter_1 (
    .count(not_1_out), .clk(clockin), .Q(counter_1_q));  // open: clr, load, up, D, carry
  not not_1 (not_1_out, counter_1_q[0]);
  not not_2 (not_2_out, counter_1_q[0]);
  T_Flip_Flop t_ff_1 (.T(1'b1), .clk(clockin), .Q(t_ff_1_q), .Qn(not_2_out));  // open: reset, preset
  T_Flip_Flop t_ff_2 (.T(t_ff_1_q), .clk(clockin), .Q(t_ff_2_q), .Qn(not_2_out));  // open: reset, preset
  and and_1 (and_1_out, t_ff_1_q, t_ff_2_q);
  T_Flip_Flop t_ff_3 (.T(and_1_out), .clk(clockin), .Q(t_ff_3_q), .Qn(not_2_out));  // open: reset, preset
  and and_2 (and_2_out, and_1_out, t_ff_3_q);
  T_Flip_Flop t_ff_4 (.T(and_2_out), .clk(clockin), .Q(t_ff_4_q), .Qn(not_2_out));  // open: reset, preset
  and and_3 (and_3_out, and_2_out, t_ff_4_q);
  T_Flip_Flop t_ff_5 (.T(and_3_out), .clk(clockin), .Q(t_ff_5_q), .Qn(not_2_out));  // open: reset, preset
  and and_4 (and_4_out, and_3_out, t_ff_5_q);
  T_Flip_Flop t_ff_6 (.T(and_4_out), .clk(clockin), .Q(t_ff_6_q), .Qn(not_2_out));  // open: reset, preset
  and and_5 (and_5_out, and_4_out, t_ff_6_q);
  T_Flip_Flop t_ff_7 (.T(and_5_out), .clk(clockin), .Q(clockout), .Qn(not_2_out));  // open: reset, preset
endmodule
