// Logisim project DD1Project2.circ as structural Verilog: 1 circuit, main circuit main
module main (
  input  reset,
  input  [2:0] in_2,
  input  [3:0] in_3,
  input  [1:0] in_4
);

  wire and_1_out, and_2_out, and_3_out, and_4_out, and_5_out, and_6_out, and_7_out, and_8_out, and_9_out,
       and_10_out, and_11_out, and_12_out, and_13_out, and_14_out, and_15_out, and_16_out,
       bcd_to_7_segment_decoder_1_p1, bcd_to_7_segment_decoder_1_p2, bcd_to_7_segment_decoder_1_p3,
       bcd_to_7_segment_decoder_1_p4, bcd_to_7_segment_decoder_1_p6, bcd_to_7_segment_decoder_1_p7,
       bcd_to_7_segment_decoder_1_p8, bcd_to_7_segment_decoder_2_p1, bcd_to_7_segment_decoder_2_p2,
       bcd_to_7_segment_decoder_2_p3, bcd_to_7_segment_decoder_2_p4, bcd_to_7_segment_decoder_2_p6,
       bcd_to_7_segment_decoder_2_p7, bcd_to_7_segment_decoder_2_p8, bcd_to_7_segment_decoder_3_p1,
       bcd_to_7_segment_decoder_3_p2, bcd_to_7_segment_decoder_3_p3, bcd_to_7_segment_decoder_3_p4,
       bcd_to_7_segment_decoder_3_p6, bcd_to_7_segment_decoder_3_p7, bcd_to_7_segment_decoder_3_p8,
       bcd_to_7_segment_decoder_4_p1, bcd_to_7_segment_decoder_4_p2, bcd_to_7_segment_decoder_4_p3,
       bcd_to_7_segment_decoder_4_p4, bcd_to_7_segment_decoder_4_p6, bcd_to_7_segment_decoder_4_p7,
       bcd_to_7_segment_decoder_4_p8, bcd_to_7_segment_decoder_5_p1, bcd_to_7_segment_decoder_5_p2,
       bcd_to_7_segment_decoder_5_p3, bcd_to_7_segment_decoder_5_p4, bcd_to_7_segment_decoder_5_p6,
       bcd_to_7_segment_decoder_5_p7, bcd_to_7_segment_decoder_5_p8, bcd_to_7_segment_decoder_6_p1,
       bcd_to_7_segment_decoder_6_p2, bcd_to_7_segment_decoder_6_p3, bcd_to_7_segment_decoder_6_p4,
       bcd_to_7_segment_decoder_6_p6, bcd_to_7_segment_decoder_6_p7, bcd_to_7_segment_decoder_6_p8, BTNC_out,
       BTND_out, BTNL_out, BTNR_out, BTNU_out, clk_out, nor_1_out, nor_2_out, not_1_out, not_2_out, or_1_out,
       or_2_out, or_3_out, or_4_out, or_5_out, or_6_out, or_7_out, or_8_out, or_9_out, or_10_out, or_11_out,
       or_12_out, t_ff_1_q, t_ff_1_qn, t_ff_2_q, t_ff_2_qn;
  wire [1:0] counter_1_q, counter_2_q, counter_3_q, multiplexer_1_out, multiplexer_2_out, multiplexer_3_out,
       multiplexer_5_out;
  wire [2:0] bcd_to_7_segment_decoder_5_p5, counter_6_q, multiplexer_7_out;
  wire [3:0] bcd_to_7_segment_decoder_3_p5, bcd_to_7_segment_decoder_4_p5, bcd_to_7_segment_decoder_6_p5,
       counter_4_q, counter_5_q, counter_7_q, counter_9_q, counter_11_q, multiplexer_4_out,
       multiplexer_6_out, multiplexer_9_out;

  or or_1 (or_1_out, BTNC_out, BTND_out);
  and and_1 (and_1_out, BTNU_out, and_3_out);
  and and_2 (and_2_out, counter_1_q[1], counter_4_q[2]);
  or or_2 (or_2_out, or_4_out, t_ff_2_qn);
  Multiplexer #(.width(2)) multiplexer_1 (.in0(in_4), .in1(counter_1_q), .out(multiplexer_1_out), .sel(t_ff_2_qn));
  Multiplexer #(.width(2)) multiplexer_2 (
    .in0(counter_2_q), .in1(counter_3_q), .out(multiplexer_2_out), .sel(BTND_out));
  and and_3 (and_3_out, counter_4_q[0], counter_4_q[3]);
  or or_3 (or_3_out, BTNL_out, BTNR_out);
  T_Flip_Flop t_ff_1 (.T(or_3_out), .clk(clk_out), .Q(t_ff_1_q), .Qn(t_ff_1_qn));  // open: reset, preset
  buf or_4 (or_4_out, and_6_out);  // OR_Gate
  Counter #(.max('h2), .width(2)) counter_1 (
    .clr(and_2_out), .load(or_1_out), .count(and_1_out), .clk(clk_out), .D(multiplexer_2_out), .Q(counter_1_q));  // open: up, carry
  Button BTNL (.out(BTNL_out));
  Counter #(.max('h2), .width(2)) counter_2 (
    .clr(reset), .load(or_2_out), .count(and_8_out), .clk(clk_out), .D(multiplexer_1_out), .Q(counter_2_q));  // open: up, carry
  Multiplexer #(.width(2)) multiplexer_3 (
    .in0(counter_2_q), .in1(counter_1_q), .out(multiplexer_3_out), .sel(t_ff_2_qn));
  not not_1 (not_1_out, BTND_out);
  Button BTNU (.out(BTNU_out));
  Button BTNC (.out(BTNC_out));
  Button BTND (.out(BTND_out));
  Clock clk (.out(clk_out));
  Button BTNR (.out(BTNR_out));
  and and_4 (and_4_out, and_8_out, counter_2_q[1]);
  Multiplexer #(.width(4)) multiplexer_4 (
    .in0(counter_5_q), .in1(counter_4_q), .out(multiplexer_4_out), .sel(t_ff_2_qn));
  LedBar #(.matrixcols(3)) ledbar_1 (.led0(t_ff_2_qn), .led1(t_ff_1_qn), .led2(t_ff_1_q));
  and and_5 (and_5_out, t_ff_1_qn, or_11_out);
  or or_5 (or_5_out, BTNC_out, and_2_out);
  Counter #(.max('h2), .width(2)) counter_3 (
    .load(BTNU_out), .up(BTNU_out), .count(and_7_out), .clk(clk_out), .D(counter_2_q), .Q(counter_3_q));  // open: clr, carry
  Multiplexer #(.width(2)) multiplexer_5 (
    .in0(multiplexer_3_out), .in1(counter_3_q), .out(multiplexer_5_out), .sel(BTND_out));
  // BCD_to_7_Segment_decoder bcd_to_7_segment_decoder_1: pin names not known; wires that end beside it: bcd_to_7_segment_decoder_1_p1, bcd_to_7_segment_decoder_1_p2, bcd_to_7_segment_decoder_1_p3, bcd_to_7_segment_decoder_1_p4, {2'b00, multiplexer_5_out}, bcd_to_7_segment_decoder_1_p6, bcd_to_7_segment_decoder_1_p7, bcd_to_7_segment_decoder_1_p8
  and and_6 (and_6_out, counter_5_q[2], counter_2_q[1]);
  or or_6 (or_6_out, t_ff_2_qn, or_7_out);
  Multiplexer #(.width(4)) multiplexer_6 (.in0(in_3), .in1(counter_4_q), .out(multiplexer_6_out), .sel(t_ff_2_qn));
  Counter #(.max('h9), .width(4)) counter_4 (
    .clr(and_2_out), .load(or_5_out), .up(BTNU_out), .count(and_5_out), .clk(clk_out), .D(counter_5_q),
    .Q(counter_4_q));  // open: carry
  and and_7 (and_7_out, nor_1_out, BTND_out);
  _7_Segment_Display u_7_segment_display_1 (
    .g(bcd_to_7_segment_decoder_1_p1), .f(bcd_to_7_segment_decoder_1_p3), .a(bcd_to_7_segment_decoder_1_p6),
    .b(bcd_to_7_segment_decoder_1_p8), .e(bcd_to_7_segment_decoder_1_p2), .d(bcd_to_7_segment_decoder_1_p4),
    .c(bcd_to_7_segment_decoder_1_p7));  // open: dp
  Counter #(.max('h9), .width(4)) counter_5 (
    .clr(reset), .load(or_6_out), .count(and_10_out), .clk(clk_out), .D(multiplexer_6_out), .Q(counter_5_q));  // open: up, carry
  or or_7 (or_7_out, and_6_out, and_8_out);
  // BCD_to_7_Segment_decoder bcd_to_7_segment_decoder_2: pin names not known; wires that end beside it: bcd_to_7_segment_decoder_2_p1, bcd_to_7_segment_decoder_2_p2, bcd_to_7_segment_decoder_2_p3, bcd_to_7_segment_decoder_2_p4, multiplexer_4_out, bcd_to_7_segment_decoder_2_p6, bcd_to_7_segment_decoder_2_p7, bcd_to_7_segment_decoder_2_p8
  nor nor_1 (nor_1_out, counter_4_q[3], counter_4_q[2], counter_4_q[1], counter_4_q[0]);
  _7_Segment_Display u_7_segment_display_2 (
    .g(bcd_to_7_segment_decoder_2_p1), .f(bcd_to_7_segment_decoder_2_p3), .a(bcd_to_7_segment_decoder_2_p6),
    .b(bcd_to_7_segment_decoder_2_p8), .e(bcd_to_7_segment_decoder_2_p2), .d(bcd_to_7_segment_decoder_2_p4),
    .c(bcd_to_7_segment_decoder_2_p7));  // open: dp
  and and_8 (and_8_out, counter_5_q[3], and_10_out, counter_5_q[0]);
  // BCD_to_7_Segment_decoder bcd_to_7_segment_decoder_3: pin names not known; wires that end beside it: bcd_to_7_segment_decoder_3_p1, bcd_to_7_segment_decoder_3_p2, bcd_to_7_segment_decoder_3_p3, bcd_to_7_segment_decoder_3_p4, bcd_to_7_segment_decoder_3_p5, bcd_to_7_segment_decoder_3_p6, bcd_to_7_segment_decoder_3_p7, bcd_to_7_segment_decoder_3_p8
  _7_Segment_Display u_7_segment_display_3 (
    .g(bcd_to_7_segment_decoder_3_p1), .f(bcd_to_7_segment_decoder_3_p3), .a(bcd_to_7_segment_decoder_3_p6),
    .b(bcd_to_7_segment_decoder_3_p8), .e(bcd_to_7_segment_decoder_3_p2), .d(bcd_to_7_segment_decoder_3_p4),
    .c(bcd_to_7_segment_decoder_3_p7));  // open: dp
  Counter #(.max('h5), .width(3)) counter_6 (
    .clr(reset), .load(or_9_out), .up(not_1_out), .count(or_8_out), .clk(clk_out), .D(multiplexer_7_out),
    .Q(counter_6_q));  // open: carry
  or or_8 (or_8_out, and_11_out, and_15_out);
  and and_9 (and_9_out, not_2_out, t_ff_2_qn);
  not not_2 (not_2_out, BTNU_out);
  or or_9 (or_9_out, and_10_out, and_9_out, and_14_out);
  and and_10 (and_10_out, counter_6_q[0], and_11_out, counter_6_q[2]);
  Multiplexer #(.width(3)) multiplexer_7 (
    .in0(in_2), .in1(counter_11_q[2:0]), .out(multiplexer_7_out), .sel(t_ff_2_qn));
  Multiplexer #(.width(4)) multiplexer_8 (
    .in0({1'b0, counter_6_q}), .in1(counter_11_q), .out(bcd_to_7_segment_decoder_3_p5), .sel(BTND_out));
  // BCD_to_7_Segment_decoder bcd_to_7_segment_decoder_4: pin names not known; wires that end beside it: bcd_to_7_segment_decoder_4_p1, bcd_to_7_segment_decoder_4_p2, bcd_to_7_segment_decoder_4_p3, bcd_to_7_segment_decoder_4_p4, bcd_to_7_segment_decoder_4_p5, bcd_to_7_segment_decoder_4_p6, bcd_to_7_segment_decoder_4_p7, bcd_to_7_segment_decoder_4_p8
  _7_Segment_Display u_7_segment_display_4 (
    .g(bcd_to_7_segment_decoder_4_p1), .f(bcd_to_7_segment_decoder_4_p3), .a(bcd_to_7_segment_decoder_4_p6),
    .b(bcd_to_7_segment_decoder_4_p8), .e(bcd_to_7_segment_decoder_4_p2), .d(bcd_to_7_segment_decoder_4_p4),
    .c(bcd_to_7_segment_decoder_4_p7));  // open: dp
  or or_10 (or_10_out, t_ff_2_qn, and_11_out);
  Counter #(.max('hf), .width(4)) counter_7 (
    .clr(reset), .load(or_10_out), .count(and_13_out), .clk(clk_out), .D(multiplexer_9_out), .Q(counter_7_q));  // open: up, carry
  Multiplexer #(.width(4)) multiplexer_9 (.in0(in_3), .in1(counter_9_q), .out(multiplexer_9_out), .sel(t_ff_2_qn));
  and and_11 (and_11_out, and_13_out, counter_7_q[3], counter_7_q[0]);
  Multiplexer #(.width(4)) multiplexer_10 (
    .in0(counter_7_q), .in1(counter_9_q), .out(bcd_to_7_segment_decoder_4_p5), .sel(t_ff_2_qn));
  // BCD_to_7_Segment_decoder bcd_to_7_segment_decoder_5: pin names not known; wires that end beside it: bcd_to_7_segment_decoder_5_p1, bcd_to_7_segment_decoder_5_p2, bcd_to_7_segment_decoder_5_p3, bcd_to_7_segment_decoder_5_p4, {1'b0, bcd_to_7_segment_decoder_5_p5}, bcd_to_7_segment_decoder_5_p6, bcd_to_7_segment_decoder_5_p7, bcd_to_7_segment_decoder_5_p8
  _7_Segment_Display u_7_segment_display_5 (
    .g(bcd_to_7_segment_decoder_5_p1), .f(bcd_to_7_segment_decoder_5_p3), .a(bcd_to_7_segment_decoder_5_p6),
    .b(bcd_to_7_segment_decoder_5_p8), .e(bcd_to_7_segment_decoder_5_p2), .d(bcd_to_7_segment_decoder_5_p4),
    .c(bcd_to_7_segment_decoder_5_p7));  // open: dp
  Counter #(.max('h7), .width(3)) counter_8 (
    .clr(reset), .load(and_13_out), .count(and_16_out), .clk(clk_out), .D(in_2),
    .Q(bcd_to_7_segment_decoder_5_p5));  // open: up, carry
  and and_12 (and_12_out, t_ff_1_q, or_11_out);
  // BCD_to_7_Segment_decoder bcd_to_7_segment_decoder_6: pin names not known; wires that end beside it: bcd_to_7_segment_decoder_6_p1, bcd_to_7_segment_decoder_6_p2, bcd_to_7_segment_decoder_6_p3, bcd_to_7_segment_decoder_6_p4, bcd_to_7_segment_decoder_6_p5, bcd_to_7_segment_decoder_6_p6, bcd_to_7_segment_decoder_6_p7, bcd_to_7_segment_decoder_6_p8
  and and_13 (and_13_out, bcd_to_7_segment_decoder_5_p5[2], and_16_out, bcd_to_7_segment_decoder_5_p5[0]);
  Counter #(.max('h9), .width(4)) counter_9 (
    .load(BTNC_out), .up(BTNU_out), .count(and_12_out), .clk(clk_out), .D(counter_7_q), .Q(counter_9_q));  // open: clr, carry
  or or_11 (or_11_out, BTNU_out, BTND_out);
  and and_14 (and_14_out, BTND_out, nor_2_out);
  _7_Segment_Display u_7_segment_display_6 (
    .g(bcd_to_7_segment_decoder_6_p1), .f(bcd_to_7_segment_decoder_6_p3), .a(bcd_to_7_segment_decoder_6_p6),
    .b(bcd_to_7_segment_decoder_6_p8), .e(bcd_to_7_segment_decoder_6_p2), .d(bcd_to_7_segment_decoder_6_p4),
    .c(bcd_to_7_segment_decoder_6_p7));  // open: dp
  Counter #(.max('hf), .width(4)) counter_10 (
    .clr(reset), .load(and_16_out), .count(t_ff_2_q), .clk(clk_out), .D(in_3),
    .Q(bcd_to_7_segment_decoder_6_p5));  // open: up, carry
  or or_12 (or_12_out, BTNC_out, BTNU_out);
  Counter #(.max('h5), .width(4)) counter_11 (
    .load(or_12_out), .up(BTNU_out), .count(and_14_out), .clk(clk_out), .D({1'b0, counter_6_q}),
    .Q(counter_11_q));  // open: clr, carry
  and and_15 (and_15_out, counter_9_q[0], BTNU_out, counter_9_q[3]);
  T_Flip_Flop t_ff_2 (.T(BTNC_out), .clk(clk_out), .Q(t_ff_2_q), .Qn(t_ff_2_qn));  // open: reset, preset
  and and_16 (and_16_out, bcd_to_7_segment_decoder_6_p5[0], bcd_to_7_segment_decoder_6_p5[3]);
  nor nor_2 (nor_2_out, counter_9_q[3], counter_9_q[2], counter_9_q[1], counter_9_q[0]);
endmodule
